// Logisim project electronic_combination_doorbell.circ as structural Verilog: 1 circuit, main circuit main
module main (
  input  B1,
  input  B2,
  input  B3,
  input  RST,
  output Q1,
  output Q0,
  output BELL
);

  wire adv3_out, and_1_out, and_3_out, and_5_out, and_6_out, CLK_out, IDLE_out, no_btn_p4, or_1_out,
       or_2_out, S1_out, S2_out, undriven, undriven_2, undriven_3;

  Clock CLK (.out(CLK_out));
  // NOR_Gate no_btn: pin names not known; wires that end beside it: B1, B2, B3, no_btn_p4
  and IDLE (IDLE_out, ~undriven, ~undriven_2);  // AND_Gate
  and S1 (S1_out, ~undriven, undriven_2);  // AND_Gate
  and S2 (S2_out, undriven, ~undriven_2);  // AND_Gate
  and UNLOCK (BELL, undriven, undriven_2);
  and and_1 (and_1_out, S1_out, B2);
  and adv3 (adv3_out, S2_out, B3);
  and and_2 (adv3_out, S2_out, no_btn_p4);
  and and_3 (and_3_out, IDLE_out, B1);
  and and_4 (adv3_out, S1_out, no_btn_p4);
  or or_1 (or_1_out, and_1_out, adv3_out, adv3_out);
  or or_2 (or_2_out, and_3_out, adv3_out, adv3_out);
  and and_5 (and_5_out, or_1_out, ~RST);  // AND_Gate
  and and_6 (and_6_out, or_2_out, ~RST);  // AND_Gate
  D_Flip_Flop Q1__MSB (.clk(and_5_out), .D(CLK_out), .Q(Q1));  // open: Qn, preset, en, reset
  D_Flip_Flop Q0__LSB (.clk(and_6_out), .D(undriven_3), .Q(Q0));  // open: Qn, preset, en, reset
  LED STATE_00__IDLE (.in(IDLE_out));
  LED STATE_01__S1__B1_Pressed (.in(S1_out));
  LED STATE_10__S2__B2_Pressed (.in(S2_out));
  LED STATE_11__UNLOCK__Sequence_Accepted (.in(BELL));
  LED BELL_CHIME__ACTIVE (.in(BELL));

  // Notes on the sheet:
  //   USER INPUTS
  //   STATE DECODER
  //   ELECTRONIC COMBINATION DOORBELL FSM (B1 -> B2 -> B3)
  //   Digital Electronics Microproject - Christ College of Engineering (Autonomous)
  //   NEXT-STATE LOGIC (D1, D0)
  //   STATE REGISTERS (D-FF)
  //   OUTPUTS & INDICATORS
endmodule
